# Fritzing sketch breadboard (saved by Fritzing 0.9.0b)
breadboards: 1

parts:
  Part1 = Arduino Uno (Rev3)
  S1 = Momentary Switch [package=ksa_sealed_tac_switch]
  LED1 = LED - 5mm [color="Blue (525nm)" package="5 mm [THT]"]
  LED2 = LED - 5mm [color="Red (633nm)" package="5 mm [THT]"]
  LED3 = LED - 5mm [color="Red (633nm)" package="5 mm [THT]"]
  LED4 = LED - 5mm [color="Red (633nm)" package="5 mm [THT]"]
  LED5 = LED - 5mm [color="Red (633nm)" package="5 mm [THT]"]
  LED6 = LED - 5mm [color="Red (633nm)" package="5 mm [THT]"]
  LED7 = LED - 5mm [color="Green (570nm)" package="5 mm [THT]"]
  S2 = Pushbutton [package="[THT]"]
  S3 = Pushbutton [package="[THT]"]
  R1 = Resistor [tolerance=±5% resistance=220 package=THT]
  R2 = Resistor [tolerance=±5% resistance=220 package=THT]
  R3 = Resistor [tolerance=±5% resistance=220 package=THT]
  R4 = Resistor [tolerance=±5% resistance=220 package=THT]

nets:
  N1: Part1.D8, LED7.anode
  N2: Part1.D9_PWM, LED4.anode
  N3: Part1.D10_PWM/SS, LED5.anode
  N4: Part1.D11_PWM/MOSI, LED6.anode
  N5: Part1.D12/MISO, Part1.D4, Part1.GND, S2.Pin_1, S2.Pin_2, S3.Pin_3, S3.Pin_4, R1.Pin_0, R2.Pin_0
  N6: Part1.D2, S1.3
  N7: Part1.D3_PWM, LED2.anode
  N8: Part1.D5_PWM, LED3.anode
  N9: Part1.D7, LED1.anode
  N10: Part1.5V, S1.4, R3.Pin_1, R4.Pin_0
  N11: S1.2, R2.Pin_1
  N12: LED1.cathode, LED2.cathode, LED3.cathode, LED4.cathode, LED5.cathode, LED6.cathode, LED7.cathode, R1.Pin_1
  N13: S2.Pin_3, S2.Pin_4, R4.Pin_1
  N14: S3.Pin_1, S3.Pin_2, R3.Pin_0
